# Fritzing sketch el_dgs (saved by Fritzing 0.8.3b)

parts:
  Mod1 = Raspberry Pi 4B
  Parte1 = Arduino Nano (Rev3.0)
  Parte2 = Arduino Nano (Rev3.0)
  M1 = BTS7960
  M2 = BTS7960
  M3 = 0.9v-5V booster usb output
  J7 = screw terminal, 3 pins
  J8 = screw terminal, 3 pins
  J9 = screw terminal, 3 pins
  J10 = screw terminal, 3 pins
  J6 = screw terminal, 10 pins
  J5 = screw terminal, 10 pins
  BAT3 = 12 battery [package=battery]
  BAT4 = 12 battery [package=battery]
  M4 = DC Motor
  M5 = DC Motor
  RE2 = KY-040 Rotary encoder [package=THT]
  RE1 = KY-040 Rotary encoder [package=THT]

nets:
  N1: Mod1.GPIO2, Parte1.A4
  N2: Mod1.GPIO3, Parte1.A5
  N3: Mod1.GND, Mod1.GPIO14
  N4: Mod1.ID_SD, Parte2.A4
  N5: Mod1.ID_SC, Mod1.GPIO12, Parte2.A5
  GND: Parte1.GND, Parte2.GND
  N6: Parte1.D2, RE1.DT
  N7: Parte1.D8, RE1.CLK
  N8: Parte1.D9, M1.pin1
  N9: Parte1.D10, M1.pin2
  N10: Parte2.D2, RE2.DT
  N11: Parte2.D8, RE2.CLK
  N12: Parte2.D9, M2.pin1
  N13: Parte2.D10, M2.pin2
  N14: M1.pin3, M1.pin5, J5.pin8
  N15: M1.pin4, J5.pin7
  N16: M1.pin7, J5.pin9
  N17: M1.pin8, J6.pin9
  N18: M1.pin9, M4.pin_2
  N19: M1.pin10, M4.pin_1
  N20: M1.pin11, J9.pin2
  N21: M1.pin12, J10.pin2
  N22: M2.pin3, M2.pin5, J5.pin5
  N23: M2.pin4, J5.pin4
  N24: M2.pin7, J5.pin6
  N25: M2.pin8, J6.pin8
  N26: M2.pin9, M5.pin_2
  N27: M2.pin10, M5.pin_1
  N28: M2.pin11, J9.pin3
  N29: M2.pin12, J10.pin3
  N30: M3.pin1, M3.pin4, J7.pin3, J6.pin10
  N31: M3.pin2, J8.pin3
  N32: M3.pin3, J5.pin10
  N33: J7.pin1, J10.pin1
  N34: J7.pin2, BAT3.-, BAT4.-
  N35: J8.pin1, J9.pin1
  N36: J8.pin2, BAT3.+, BAT4.+
  N37: J6.pin6, RE2.GND
  N38: J6.pin7, RE1.GND
  N39: J5.pin2, RE2.Vcc
  N40: J5.pin3, RE1.Vcc

notes:
  FUENTE DE ALIMENTACIÓN - 12V 18A
  REGULADOR DE VOLTAJE DC-DC 5V
  PUENTES H
  (MODULOS BTS7960)
  MOTOR DERECHO
  MOTOR IZQUIERDO
  MICROCONTROLADOR (ARDUINO NANO)
  ORDENADOR (RASPBERRI PI 4B)

custom parts:
  BTS7960: BTS7960 43A Peak Power H-Bridge PWM Motor Driver
  0.9v-5V booster usb output: 0.9 V ~ 5 V up 5 V DC - DC booster module.
  12 battery: 12V lead acid type battery, like the Husqvarna YTH2448 12V 35AH battery. This is the mini version 1/4 the size of the actual battery to be closer to typical breadboard parts (around 2in wide rathher than 7in). The pads in pcb are sized to accomidate up to 14ga wire (as these batterys will deliver high currents.)
  KY-040 Rotary encoder: KY-040 Rotary Encoder with switch on breakout borad from AZ Delivery
